# Fritzing sketch Babycakes (saved by Fritzing 1.0.2b)

parts:
  PDH1 = rev_pdh
  BLDC1 = CTRE Falcon 500 [part_number=19-708850]
  BLDC2 = CTRE Falcon 500 [part_number=19-708850]
  BLDC3 = CTRE Falcon 500 [part_number=19-708850]
  BLDC4 = CTRE Falcon 500 [part_number=19-708850]
  BLDC5 = REV NEO 550 BLDC Motor [part_number=REV-21-1651]
  ctrl1 = rev_spark_max [part_number=rev-11-2158]
  BLDC6 = REV NEO 550 BLDC Motor [part_number=REV-21-1651]
  ctrl1_2 = rev_spark_max [part_number=rev-11-2158]
  BLDC7 = REV NEO 550 BLDC Motor [part_number=REV-21-1651]
  ctrl1_3 = rev_spark_max [part_number=rev-11-2158]
  BLDC8 = REV NEO 550 BLDC Motor [part_number=REV-21-1651]
  ctrl1_4 = rev_spark_max [part_number=rev-11-2158]
  Mini_Power_Module1 = REV Mini Power Module [form="♀ (female)" package=THT]  # not connected

nets:
  N1: PDH1.connector4, ctrl1_4.connector0
  N2: PDH1.connector5, ctrl1_4.connector1
  N3: PDH1.connector6, BLDC3.Vin+
  N4: PDH1.connector7, BLDC3.Vin-
  N5: PDH1.connector8, ctrl1_3.connector0
  N6: PDH1.connector9, ctrl1_3.connector1
  N7: PDH1.connector10, BLDC4.Vin+
  N8: PDH1.connector11, BLDC4.Vin-
  N9: PDH1.connector12, ctrl1_2.connector0
  N10: PDH1.connector13, ctrl1_2.connector1
  N11: PDH1.connector14, BLDC2.Vin+
  N12: PDH1.connector15, BLDC2.Vin-
  N13: PDH1.connector16, ctrl1.connector0
  N14: PDH1.connector17, ctrl1.connector1
  N15: PDH1.connector18, BLDC1.Vin+
  N16: PDH1.connector19, BLDC1.Vin-
  N17: BLDC5.A, ctrl1.connector18
  N18: BLDC5.B, ctrl1.connector2
  N19: BLDC5.C, ctrl1.connector3
  N20: BLDC6.A, ctrl1_2.connector18
  N21: BLDC6.B, ctrl1_2.connector2
  N22: BLDC6.C, ctrl1_2.connector3
  N23: BLDC7.A, ctrl1_3.connector18
  N24: BLDC7.B, ctrl1_3.connector2
  N25: BLDC7.C, ctrl1_3.connector3
  N26: BLDC8.A, ctrl1_4.connector18
  N27: BLDC8.B, ctrl1_4.connector2
  N28: BLDC8.C, ctrl1_4.connector3

custom parts:
  CTRE Falcon 500: The Falcon 500 powered by Talon FX is a brushless motor with an integrated motor controller and high-resolution encoder, custom designed specifically for the FIRST Robotics Competition, through a collaboration between Cross the Road Electronics and VEX Robotics.
  REV NEO 550 BLDC Motor: The REV NEO 550 Brushless Motor is the newest member in the NEO family of brushless motors. Its output power and small size are specifically designed to make NEO 550 the perfect motor for intakes and other non-drivetrain robot mechanisms. Mounting holes and pilot match a standard 550 series motor, making it natively mount to many existing off-the-shelf gearboxes.
  REV Mini Power Module: Generic female header
