# Fritzing sketch Electrical Diagram (saved by Fritzing 1.0.2b)
breadboards: 1

parts:
  CAM1 = Limelight 2plus
  NetSw1 = Brainboxes Ethernet Switch [part_number=SW-005 package="DIN 101x101mm"]

nets:
  N1: CAM1.ETH0, NetSw1.eth1

custom parts:
  Limelight 2plus: Limelight makes reliable FRC vision accessible to all teams, regardless of programming ability and time constraints. Vision has never been easier. Limelight 2+ takes the Einstein-proven Limelight 2 and perfects it. Its internals have been redesigned to: - Reduce power consumption by up to 50% - Eliminate the LED "warm-up" period. - Further improve low voltage performance, dropping the brownout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
  Brainboxes Ethernet Switch: Light Industrial/Commercial Ethernet 5 Port unmanaged switch. Galvanically Isolated Ports. Power supply with wide voltage range means it can be powered from USB or on the 24V factory floor. Power terminal is removable with for easy wiring. Power consumption is optimised based on the status of the link device. No software required. Ideal for factory floor, in vehicle and marine applications.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
